// Logisim project project-1.circ as structural Verilog: 2 circuits, main circuit main
module main (
  output [31:0] out_1
);

  assign out_1 = {32{1'b1}} & 32'hf0f0f0f;  // AND_Gate and_1, 32 bits wide
endmodule

module ALU_32 (
  input  [31:0] A,
  input  [31:0] B
);

  Adder #(.width(32)) adder_1 (.a(A), .b(B));  // open: out, cin, cout
  Adder #(.width(32)) adder_2 (.a(A), .b(32'h1));  // open: out, cin, cout
  Subtractor #(.width(32)) subtractor_1 (.a(A), .b(B));  // open: out, bin, bout
  Multiplier #(.width(32)) multiplier_1 (.a(A), .b(B));  // open: out, cin, cout
  Shifter #(.width(32)) shifter_1 (.in(A), .\dist (B[4:0]));  // open: out
  Shifter #(.width(32), .shift("lr")) shifter_2 (.in(A), .\dist (B[4:0]));  // open: out
  // AND_Gate and_1 has open pins: in0=A, in1=B, out=open
  // OR_Gate or_1 has open pins: in0=A, in1=B, out=open

  // Notes on the sheet:
  //   Adder-32
  //   A + 1
  //   A - B
  //   Mult
  //   Shift Left
  //   Shift Right
  //   AND-32
  //   OR-32
endmodule
