// Logisim project prj-3.circ as structural Verilog: 1 circuit, main circuit main
module main (
  output [31:0] out_1
);

  wire Clock, Clr;

  Counter #(.width(32), .max('hffffffff)) counter_1 (
    .load(1'b0), .count(1'b1), .Q(out_1), .clk(Clock), .clr(Clr));  // open: D, carry
  Clock clock_1 (.out(Clock));
  Button button_1 (.out(Clr));

  // Notes on the sheet:
  //   Counter
endmodule
